# Fritzing sketch fase2 (saved by Fritzing 0.8.7b)
breadboards: 1

parts:
  U1 = ESP32-38PinWide [part_number=ESP32-38PinWide]
  R1 = Resistor [tolerance=±5% package="0402 [SMD]"]
  LED2 = smd LED [color="Red (633nm)" package="0603 [SMD]"]
  Q1 = NPN-Transistor [package="TO92 [THT]"]
  U2 = ESP32-38PinWide [part_number=ESP32-38PinWide]
  R2 = Resistor [tolerance=±5% resistance=220 package=THT]
  LED3 = LED - 5mm [color="Red (633nm)" package="5 mm [THT]"]  # not connected
  R3 = Resistor [tolerance=±5% package="0402 [SMD]"]
  IC2_D = TL074 Quad Opamp (Movable) [package="DIP (Dual Inline)"]  # not connected
  IC2 = TL074 Quad Opamp (Movable) [package="DIP (Dual Inline)"]
  IC2_C = TL074 Quad Opamp (Movable) [package="DIP (Dual Inline)"]  # not connected
  IC2_B = TL074 Quad Opamp (Movable) [package="DIP (Dual Inline)"]  # not connected
  IC2_A = TL074 Quad Opamp (Movable) [package="DIP (Dual Inline)"]  # not connected
  IC2_PWR = TL074 Quad Opamp (Movable) [package="DIP (Dual Inline)"]  # not connected
  R4 = Resistor [package="2010 [SMD]"]

nets:
  N1: U1.3.3, R1.Pin_0
  N2: U1.GND, Q1.E, IC2.connector9
  N3: U1.GPIO16, R2.Pin_1
  N4: R1.Pin_1, LED2.cathode
  N5: LED2.anode, Q1.C
  N6: Q1.B, R2.Pin_0
  N7: U2.GPIO27, IC2.connector7, R4.Pin_0
  N8: U2.GND, R3.Pin_0
  N9: R3.Pin_1, IC2.connector8, R4.Pin_1

notes:
  Fotodetetor
  R(IR LED) = (3.3-1.6)/20mA
  = 160 Ω
  R(Base NPN) = (3.3-0.6)/1.35mA
  = 2k Ω
  I(Base NPN) = (3.3-0.6)/2k
  = 1.35 mA
  -3.3V
  +5V
  +3.3V

custom parts:
  ESP32-38PinWide: Generic 38-Pin ESP32 with wide format (only access to one side of pins on a breadboard) based on Stephen Lilley's HiLetgo ESP-WROOM-32 ESP32 ESP-32S Development Board.
  TL074 Quad Opamp (Movable): Quadruple Operational Amplifier (Opamp)
  TL074 Quad Opamp (Movable): Quadruple Operational Amplifier (Opamp)
  TL074 Quad Opamp (Movable): Quadruple Operational Amplifier (Opamp)
  TL074 Quad Opamp (Movable): Quadruple Operational Amplifier (Opamp)
  TL074 Quad Opamp (Movable): Quadruple Operational Amplifier (Opamp)
  TL074 Quad Opamp (Movable): Quadruple Operational Amplifier (Opamp)
